// Logisim project G2.circ as structural Verilog: 14 circuits, main circuit main
module main (
  output [31:0] Jump_Address,
  output [31:0] Fetched_Instruction,
  output [31:0] A,
  output [31:0] B,
  output [31:0] B_2,
  output [31:0] Result,
  output [31:0] Next_Instruction,
  output [31:0] B_3,
  output [31:0] Data,
  output [5:0] Operation_Code,
  output [31:0] A_2,
  output [31:0] B_4,
  output [31:0] Result_2,
  output [31:0] Write_Back,
  output [15:0] out_15,
  output [31:0] _0_15,
  output [3:0] out_17,
  output [31:0] _0_15_2,
  output [3:0] out_19,
  output [2:0] out_20,
  output [1:0] out_21,
  output [1:0] out_22,
  output [1:0] out_23,
  output [1:0] out_24
);

  wire ALUSrc, Branch, BranchTaken, ex_mem_1_memread__out, ex_mem_1_memtoreg__out, ex_mem_1_memwrite__out,
       ex_mem_1_regwrite__out, forwarding_unit_mem_1_memdatasrc__out, hazard_detection_unit_1_if_idwrite,
       hazard_detection_unit_1_mux, hazard_detection_unit_1_pcwrite, id_ex_1_alusrc__out,
       id_ex_1_memread__out, id_ex_1_memtoreg__out, id_ex_1_memwrite__out, id_ex_1_regwrite__out, JAL,
       JumpReg, mem_wb_1_memtoreg__out, mem_wb_1_regwrite__out, MemRead, MemToReg, MemWrite, nor_1_out,
       not_1_out, not_2_out, or_1_out, RegDst, RegWrite, Tick;
  wire [1:0] ALUOp, id_ex_1_aluop__out;
  wire [3:0] mips_alu_1_p3;
  wire [4:0] ex_mem_1_regdest__out, id_ex_1_regdest__out, id_ex_1_rs__out, id_ex_1_rt__out,
       mem_wb_1_regdest__out, multiplexer_5_out, multiplexer_7_out, multiplexer_10_out;
  wire [5:3] id_ex_1_opcode__out;
  wire [6:0] multiplexer_9_out;
  wire [23:0] bit_extender_3_out;
  wire [27:0] bit_extender_1_out, if_id_1_pc__out;
  wire [31:0] adder_1_p3, adder_2_p4, branch_1_out, ex_mem_1_inst___out, id_ex_1_a__out,
       if_id_1_return_adress__out, mem_wb_1_address__out, mem_wb_1_read_data__out, mips_alu_1_p2,
       multiplexer_1_out, multiplexer_2_out, multiplexer_3_out, multiplexer_4_out, multiplexer_6_out,
       multiplexer_8_out, multiplexer_11_out, multiplexer_12_out, multiplexer_15_out, PC_q,
       registerfile_1_p9, undriven;

  Multiplexer #(.width(32), .enable("false")) multiplexer_1 (
    .in0(multiplexer_2_out), .in1(adder_1_p3), .out(multiplexer_1_out), .sel(nor_1_out));
  nor nor_1 (nor_1_out, JAL, JumpReg, BranchTaken);
  Register #(.width(32)) PC (
    .D(multiplexer_1_out), .en(hazard_detection_unit_1_pcwrite), .Q(PC_q), .clk(Tick));  // open: clr
  // Adder adder_1: pin names not known; wires that end beside it: PC_q, 32'h4, adder_1_p3
  // Adder adder_2: pin names not known; wires that end beside it: PC_q, 32'h8, PC_q, adder_2_p4
  Clock clock_1 (.out(Tick));
  // MIPSProgramROM mipsprogramrom_1: pin names not known; wires that end beside it: Next_Instruction
  IF_ID if_id_1 (
    .Clock(Tick), .PC__in(adder_1_p3), .Inst___in(Next_Instruction),
    .PC__out({Jump_Address[31:28], if_id_1_pc__out}), .Inst___out(Fetched_Instruction),
    .Return_Adress__in(adder_2_p4), .Return_Adress__out(if_id_1_return_adress__out),
    .Stall(hazard_detection_unit_1_if_idwrite));
  Hazard_detection_unit hazard_detection_unit_1 (
    .PCWrite(hazard_detection_unit_1_pcwrite), .IF_IDWrite(hazard_detection_unit_1_if_idwrite),
    .MUX(hazard_detection_unit_1_mux), .IF_ID_RegisterRt(Fetched_Instruction[20:16]),
    .IF_ID_RegisterRs(Fetched_Instruction[25:21]), .ID_EX_MemRead(id_ex_1_memread__out),
    .ID_EX_RegisterRt(id_ex_1_rt__out));
  // PLA Control: pin names not known; wires that end beside it: Fetched_Instruction[31:26]
  Hazard_detection_unit__branch hazard_detection_unit_branch_1 ();  // open: in_1, PCWrite
  Multiplexer #(.width(32), .enable("false")) multiplexer_2 (
    .in0(multiplexer_4_out), .in1(A), .out(multiplexer_2_out), .sel(JumpReg));
  Comparator #(.mode("unsigned")) comparator_1 (.a({ALUOp, _0_15[5:0]}), .b(8'h88), .eq(JumpReg));  // open: gt, lt
  assign bit_extender_1_out = {{2{1'b0}}, Fetched_Instruction[25:0]};  // Bit_Extender bit_extender_1
  Multiplexer #(.width(32), .enable("false")) multiplexer_3 (
    .in0(if_id_1_return_adress__out), .in1(B_3), .out(multiplexer_3_out), .sel(not_1_out));
  not not_1 (not_1_out, JAL);
  Multiplexer #(.width(32), .enable("false")) multiplexer_4 (
    .in0(branch_1_out), .in1(Jump_Address), .out(multiplexer_4_out), .sel(JAL));
  or or_1 (or_1_out, mem_wb_1_regwrite__out, JAL);
  Multiplexer #(.width(5), .enable("false")) multiplexer_5 (
    .in0(mem_wb_1_regdest__out), .in1(multiplexer_10_out), .out(multiplexer_5_out), .sel(JAL));
  Shifter #(.width(28)) shifter_1 (.in(bit_extender_1_out), .\dist (5'b00010), .out(Jump_Address[27:0]));
  // RegisterFile registerfile_1: pin names not known; wires that end beside it: multiplexer_3_out, Tick, or_1_out, multiplexer_5_out, Fetched_Instruction[25:21], Fetched_Instruction[20:16], A, B, registerfile_1_p9
  assign _0_15 = {{16{Fetched_Instruction[15]}}, Fetched_Instruction[15:0]};  // Bit_Extender bit_extender_2
  Forwarding_Unit__ID forwarding_unit_id_1 (
    .rs__A__in(Fetched_Instruction[25:21]), .rt__B__in(Fetched_Instruction[20:16]),
    .ID_EX_RegDest__in(id_ex_1_regdest__out), .EX_MEM_RegDest__in(ex_mem_1_regdest__out),
    .ID_EX_RegWrite__in(id_ex_1_regwrite__out), .EX_MEM_RegWrite__in(ex_mem_1_regwrite__out),
    .MEM_WB_RegWrite__in(mem_wb_1_regwrite__out), .MEM_WB_RegDest__in(mem_wb_1_regdest__out),
    .B__out(out_24), .A__out(out_23));
  Branch branch_1 (
    .A__in(multiplexer_6_out), .B__in(multiplexer_8_out), .PC__in({Jump_Address[31:28], if_id_1_pc__out}),
    .immediate__in(_0_15), .Out(branch_1_out), .Branch(Branch), .BranchTaken(BranchTaken));
  Multiplexer #(.select(2), .width(32), .enable("false")) multiplexer_6 (
    .in0(A), .in1(registerfile_1_p9), .in2(A_2), .in3(B_3), .out(multiplexer_6_out), .sel(out_23));
  Multiplexer #(.width(5), .enable("false")) multiplexer_7 (
    .in0(Fetched_Instruction[20:16]), .in1(Fetched_Instruction[15:11]), .out(multiplexer_7_out), .sel(RegDst));
  Multiplexer #(.select(2), .width(32), .enable("false")) multiplexer_8 (
    .in0(B), .in1(undriven), .in2(A_2), .in3(B_3), .out(multiplexer_8_out), .sel(out_24));
  Multiplexer #(.width(7), .enable("false")) multiplexer_9 (
    .in0({ALUOp, ALUSrc, MemWrite, MemRead, RegWrite, MemToReg}), .in1({7{1'b0}}), .out(multiplexer_9_out),
    .sel(hazard_detection_unit_1_mux));
  Multiplexer #(.width(5), .enable("false")) multiplexer_10 (
    .in0(multiplexer_7_out), .in1({5{1'b1}}), .out(multiplexer_10_out), .sel(JAL));
  ID_EX id_ex_1 (
    .Clock(Tick), .A__in(A), .B__in(B), .Inst___in(_0_15), .A__out(id_ex_1_a__out), .B__out(B_2),
    .inst___out(_0_15_2), .MemToReg__in(multiplexer_9_out[0]), .MemToReg__out(id_ex_1_memtoreg__out),
    .MemRead__in(multiplexer_9_out[2]), .MemRead__out(id_ex_1_memread__out),
    .MemWrite__in(multiplexer_9_out[3]), .MemWrite__out(id_ex_1_memwrite__out),
    .ALUSrc__in(multiplexer_9_out[4]), .ALUSrc__out(id_ex_1_alusrc__out), .ALUOp__in(multiplexer_9_out[6:5]),
    .ALUOp__out(id_ex_1_aluop__out), .RegWrite__in(multiplexer_9_out[1]),
    .RegWrite__out(id_ex_1_regwrite__out), .regdest__in(multiplexer_10_out),
    .regdest__out(id_ex_1_regdest__out), .opcode__in(Fetched_Instruction[31:26]),
    .opcode__out({id_ex_1_opcode__out, out_20}), .rs__in(Fetched_Instruction[25:21]),
    .rs__out(id_ex_1_rs__out), .rt__in(Fetched_Instruction[20:16]), .rt__out(id_ex_1_rt__out));
  Multiplexer #(.select(2), .width(32), .enable("false")) multiplexer_11 (
    .in0(id_ex_1_a__out), .in1(B_3), .in2(A_2), .out(multiplexer_11_out), .sel(out_22));  // open: in3
  Multiplexer #(.select(2), .width(32), .enable("false")) multiplexer_12 (
    .in0(B_2), .in1(B_3), .in2(A_2), .out(multiplexer_12_out), .sel(out_21));  // open: in3
  ALU_control alu_control_1 (.in_1({id_ex_1_aluop__out, _0_15_2[5:0]}), .out_2(out_19));
  Forwarding_Unit__EX forwarding_unit_ex_1 (
    .A__out(out_22), .B__out(out_21), .rs__in(id_ex_1_rs__out), .rt__in(id_ex_1_rt__out),
    .MEM_WB_RegisterRd(mem_wb_1_regdest__out), .EX_MEM_RegisterRd(ex_mem_1_regdest__out),
    .EX_MEM_RegWrite__in(ex_mem_1_regwrite__out), .MEM_WB_RegWrite__in(mem_wb_1_regwrite__out));
  // MIPS_ALU mips_alu_1: pin names not known; wires that end beside it: multiplexer_11_out, mips_alu_1_p2, mips_alu_1_p3, Result
  Multiplexer #(.width(32), .enable("false")) multiplexer_13 (
    .in0(multiplexer_12_out), .in1(_0_15_2), .out(mips_alu_1_p2), .sel(id_ex_1_alusrc__out));
  Multiplexer #(.width(4), .enable("false")) multiplexer_14 (
    .in0(out_19), .in1(out_17), .out(mips_alu_1_p3), .sel(out_19[3]));
  Imm__Ctrl imm_ctrl_1 (.in_1(out_20), .out_2(out_17));
  EX_MEM ex_mem_1 (
    .Clock(Tick), .Result__in(Result), .Inst___in(B_2), .Result__out(A_2), .inst___out(ex_mem_1_inst___out),
    .MemToReg__in(id_ex_1_memtoreg__out), .MemToReg__out(ex_mem_1_memtoreg__out),
    .MemRead__in(id_ex_1_memread__out), .MemRead__out(ex_mem_1_memread__out),
    .MemWrite__in(id_ex_1_memwrite__out), .MemWrite__out(ex_mem_1_memwrite__out),
    .RegWrite__in(id_ex_1_regwrite__out), .RegWrite__out(ex_mem_1_regwrite__out),
    .RegDest__in(id_ex_1_regdest__out), .RegDest__out(ex_mem_1_regdest__out));
  Bit_Extender #(.in_width(32), .out_width(24)) bit_extender_3 (.in(A_2), .out(bit_extender_3_out));
  Multiplexer #(.width(32), .enable("false")) multiplexer_15 (
    .in0(ex_mem_1_inst___out), .in1(B_3), .out(multiplexer_15_out),
    .sel(forwarding_unit_mem_1_memdatasrc__out));
  Forwarding_Unit__MEM forwarding_unit_mem_1 (
    .WB_MemToReg__in(mem_wb_1_regwrite__out), .WB_Address__in(mem_wb_1_regdest__out),
    .MemDataSrc__out(forwarding_unit_mem_1_memdatasrc__out), .MEM_Address__in(ex_mem_1_regdest__out));
  // MIPS_RAM mips_ram_1: pin names not known; wires that end beside it: bit_extender_3_out, multiplexer_15_out, ex_mem_1_memwrite__out, ex_mem_1_memread__out, Tick, Data
  MEM_WB mem_wb_1 (
    .Clock(Tick), .Read_Data__in(Data), .Address__in(A_2), .Read_Data__out(mem_wb_1_read_data__out),
    .Address__out(mem_wb_1_address__out), .MemToReg__in(ex_mem_1_memtoreg__out),
    .MemToReg__out(mem_wb_1_memtoreg__out), .RegWrite__in(ex_mem_1_regwrite__out),
    .RegWrite__out(mem_wb_1_regwrite__out), .RegDest__in(ex_mem_1_regdest__out),
    .RegDest__out(mem_wb_1_regdest__out));
  not not_2 (not_2_out, mem_wb_1_memtoreg__out);
  Multiplexer #(.width(32), .enable("false")) multiplexer_16 (
    .in0(mem_wb_1_read_data__out), .in1(mem_wb_1_address__out), .out(B_3), .sel(not_2_out));

  assign B_4 = B_2;
  assign Operation_Code = Fetched_Instruction[31:26];
  assign out_15 = Fetched_Instruction[15:0];
  assign Result_2 = A_2;
  assign Write_Back = B_3;
endmodule

module ALU_control (
  input  [7:0] in_1,
  output [3:0] out_2
);

  // PLA pla_1: pin names not known; wires that end beside it: in_1, out_2
endmodule

module Imm__Ctrl (
  input  [2:0] in_1,
  output [3:0] out_2
);

  // PLA Imm__Ctrl: pin names not known; wires that end beside it: in_1, out_2
endmodule

module IF_ID (
  input  Clock,
  input  [31:0] PC__in,
  input  [31:0] Inst___in,
  input  [31:0] Return_Adress__in,
  input  Stall,
  output [31:0] PC__out,
  output [31:0] Inst___out,
  output [31:0] Return_Adress__out
);

  wire not_1_out;

  not not_1 (not_1_out, Stall);
  Register #(.width(32)) register_1 (.D(PC__in), .en(not_1_out), .Q(PC__out), .clk(Clock));  // open: clr
  Register #(.width(32)) register_2 (.D(Inst___in), .en(not_1_out), .Q(Inst___out), .clk(Clock));  // open: clr
  Register #(.width(32)) register_3 (
    .D(Return_Adress__in), .en(not_1_out), .Q(Return_Adress__out), .clk(Clock));  // open: clr

  // Other names for the same wires on the sheet: Tick = Clock
endmodule

module ID_EX (
  input  Clock,
  input  [31:0] A__in,
  input  [31:0] B__in,
  input  [31:0] Inst___in,
  input  [5:0] opcode__in,
  input  [4:0] regdest__in,
  input  [4:0] rs__in,
  input  [4:0] rt__in,
  input  MemToReg__in,
  input  RegWrite__in,
  input  MemRead__in,
  input  MemWrite__in,
  input  ALUSrc__in,
  input  [1:0] ALUOp__in,
  output [31:0] A__out,
  output [31:0] B__out,
  output [31:0] inst___out,
  output [5:0] opcode__out,
  output [4:0] regdest__out,
  output [4:0] rs__out,
  output [4:0] rt__out,
  output MemToReg__out,
  output RegWrite__out,
  output MemRead__out,
  output MemWrite__out,
  output ALUSrc__out,
  output [1:0] ALUOp__out
);

  Register #(.width(32)) register_1 (.D(A__in), .Q(A__out), .clk(Clock));  // open: en, clr
  Register #(.width(32)) register_2 (.D(B__in), .Q(B__out), .clk(Clock));  // open: en, clr
  Register #(.width(32)) register_3 (.D(Inst___in), .Q(inst___out), .clk(Clock));  // open: en, clr
  Register #(.width(6)) register_4 (.D(opcode__in), .Q(opcode__out), .clk(Clock));  // open: en, clr
  Register #(.width(5)) register_5 (.D(regdest__in), .Q(regdest__out), .clk(Clock));  // open: en, clr
  Register #(.width(5)) register_6 (.D(rs__in), .Q(rs__out), .clk(Clock));  // open: en, clr
  Register #(.width(5)) register_7 (.D(rt__in), .Q(rt__out), .clk(Clock));  // open: en, clr
  Register #(.width(1)) register_8 (.D(MemToReg__in), .Q(MemToReg__out), .clk(Clock));  // open: en, clr
  Register #(.width(1)) register_9 (.D(RegWrite__in), .Q(RegWrite__out), .clk(Clock));  // open: en, clr
  Register #(.width(1)) register_10 (.D(MemRead__in), .Q(MemRead__out), .clk(Clock));  // open: en, clr
  Register #(.width(1)) register_11 (.D(MemWrite__in), .Q(MemWrite__out), .clk(Clock));  // open: en, clr
  Register #(.width(1)) register_12 (.D(ALUSrc__in), .Q(ALUSrc__out), .clk(Clock));  // open: en, clr
  Register #(.width(2)) register_13 (.D(ALUOp__in), .Q(ALUOp__out), .clk(Clock));  // open: en, clr

  // Other names for the same wires on the sheet: Tick = Clock

  // Notes on the sheet:
  //   WB
  //   M
  //   EX
endmodule

module EX_MEM (
  input  Clock,
  input  [31:0] Result__in,
  input  [31:0] Inst___in,
  input  [4:0] RegDest__in,
  input  MemToReg__in,
  input  RegWrite__in,
  input  MemRead__in,
  input  MemWrite__in,
  output [31:0] Result__out,
  output [31:0] inst___out,
  output [4:0] RegDest__out,
  output MemToReg__out,
  output RegWrite__out,
  output MemRead__out,
  output MemWrite__out
);

  Register #(.width(32)) register_1 (.D(Result__in), .Q(Result__out), .clk(Clock));  // open: en, clr
  Register #(.width(32)) register_2 (.D(Inst___in), .Q(inst___out), .clk(Clock));  // open: en, clr
  Register #(.width(5)) register_3 (.D(RegDest__in), .Q(RegDest__out), .clk(Clock));  // open: en, clr
  Register #(.width(1)) register_4 (.D(MemToReg__in), .Q(MemToReg__out), .clk(Clock));  // open: en, clr
  Register #(.width(1)) register_5 (.D(RegWrite__in), .Q(RegWrite__out), .clk(Clock));  // open: en, clr
  Register #(.width(1)) register_6 (.D(MemRead__in), .Q(MemRead__out), .clk(Clock));  // open: en, clr
  Register #(.width(1)) register_7 (.D(MemWrite__in), .Q(MemWrite__out), .clk(Clock));  // open: en, clr

  // Other names for the same wires on the sheet: Tick = Clock

  // Notes on the sheet:
  //   WB
  //   M
endmodule

module MEM_WB (
  input  Clock,
  input  [31:0] Read_Data__in,
  input  [31:0] Address__in,
  input  [4:0] RegDest__in,
  input  MemToReg__in,
  input  RegWrite__in,
  output [31:0] Read_Data__out,
  output [31:0] Address__out,
  output [4:0] RegDest__out,
  output MemToReg__out,
  output RegWrite__out
);

  Register #(.width(32)) register_1 (.D(Read_Data__in), .Q(Read_Data__out), .clk(Clock));  // open: en, clr
  Register #(.width(32)) register_2 (.D(Address__in), .Q(Address__out), .clk(Clock));  // open: en, clr
  Register #(.width(5)) register_3 (.D(RegDest__in), .Q(RegDest__out), .clk(Clock));  // open: en, clr
  Register #(.width(1)) register_4 (.D(MemToReg__in), .Q(MemToReg__out), .clk(Clock));  // open: en, clr
  Register #(.width(1)) register_5 (.D(RegWrite__in), .Q(RegWrite__out), .clk(Clock));  // open: en, clr

  // Other names for the same wires on the sheet: Tick = Clock

  // Notes on the sheet:
  //   WB
endmodule

module Forwarding_Unit__EX (
  input  [4:0] EX_MEM_RegisterRd,
  input  [4:0] MEM_WB_RegisterRd,
  input  [4:0] rs__in,
  input  [4:0] rt__in,
  input  EX_MEM_RegWrite__in,
  input  MEM_WB_RegWrite__in,
  output [1:0] A__out,
  output [1:0] B__out
);

  wire and_1_out, and_6_out, comparator_1_eq, comparator_2_eq, comparator_3_eq, comparator_4_eq,
       comparator_5_eq, comparator_6_eq, comparator_7_eq, comparator_8_eq, comparator_9_eq, comparator_10_eq,
       comparator_11_eq, comparator_12_eq, nand_1_out, nand_2_out, not_1_out, not_2_out, not_3_out,
       not_4_out, not_5_out, not_6_out, not_7_out, not_8_out;

  Comparator #(.width(5), .mode("unsigned")) comparator_1 (
    .a(EX_MEM_RegisterRd), .b({5{1'b0}}), .eq(comparator_1_eq));  // open: gt, lt
  not not_1 (not_1_out, comparator_1_eq);
  Comparator #(.width(5), .mode("unsigned")) comparator_2 (
    .a(EX_MEM_RegisterRd), .b(rs__in), .eq(comparator_2_eq));  // open: gt, lt
  Comparator #(.width(5), .mode("unsigned")) comparator_3 (
    .a(EX_MEM_RegisterRd), .b({5{1'b0}}), .eq(comparator_3_eq));  // open: gt, lt
  Comparator #(.width(5), .mode("unsigned")) comparator_4 (
    .a(EX_MEM_RegisterRd), .b(rs__in), .eq(comparator_4_eq));  // open: gt, lt
  nand nand_1 (nand_1_out, not_1_out, EX_MEM_RegWrite__in);
  not not_2 (not_2_out, comparator_2_eq);
  Comparator #(.width(5), .mode("unsigned")) comparator_5 (
    .a(MEM_WB_RegisterRd), .b(rs__in), .eq(comparator_5_eq));  // open: gt, lt
  not not_3 (not_3_out, comparator_3_eq);
  Comparator #(.width(5), .mode("unsigned")) comparator_6 (
    .a(MEM_WB_RegisterRd), .b({5{1'b0}}), .eq(comparator_6_eq));  // open: gt, lt
  not not_4 (not_4_out, comparator_6_eq);
  and and_1 (and_1_out, nand_1_out, not_2_out);
  and and_2 (A__out[1], EX_MEM_RegWrite__in, not_3_out, comparator_4_eq);
  and and_3 (A__out[0], MEM_WB_RegWrite__in, not_4_out, and_1_out, comparator_5_eq);
  Comparator #(.width(5), .mode("unsigned")) comparator_7 (
    .a(EX_MEM_RegisterRd), .b({5{1'b0}}), .eq(comparator_7_eq));  // open: gt, lt
  not not_5 (not_5_out, comparator_7_eq);
  Comparator #(.width(5), .mode("unsigned")) comparator_8 (
    .a(EX_MEM_RegisterRd), .b(rt__in), .eq(comparator_8_eq));  // open: gt, lt
  Comparator #(.width(5), .mode("unsigned")) comparator_9 (
    .a(EX_MEM_RegisterRd), .b({5{1'b0}}), .eq(comparator_9_eq));  // open: gt, lt
  Comparator #(.width(5), .mode("unsigned")) comparator_10 (
    .a(EX_MEM_RegisterRd), .b(rt__in), .eq(comparator_10_eq));  // open: gt, lt
  Comparator #(.width(5), .mode("unsigned")) comparator_11 (
    .a(MEM_WB_RegisterRd), .b({5{1'b0}}), .eq(comparator_11_eq));  // open: gt, lt
  nand nand_2 (nand_2_out, not_5_out, EX_MEM_RegWrite__in);
  not not_6 (not_6_out, comparator_8_eq);
  Comparator #(.width(5), .mode("unsigned")) comparator_12 (
    .a(MEM_WB_RegisterRd), .b(rt__in), .eq(comparator_12_eq));  // open: gt, lt
  not not_7 (not_7_out, comparator_9_eq);
  and and_4 (B__out[1], EX_MEM_RegWrite__in, not_7_out, comparator_10_eq);
  not not_8 (not_8_out, comparator_11_eq);
  and and_5 (B__out[0], MEM_WB_RegWrite__in, not_8_out, and_6_out, comparator_12_eq);
  and and_6 (and_6_out, nand_2_out, not_6_out);

  // Other names for the same wires on the sheet: EX_MEM_RegWrite = EX_MEM_RegWrite__in;
  //   ID_EX_RegisterRs[4:0] = rs__in; ID_EX_RegisterRt[4:0] = rt__in; MEM_WB_RegWrite = MEM_WB_RegWrite__in
endmodule

module Hazard_detection_unit (
  input  ID_EX_MemRead,
  input  [4:0] ID_EX_RegisterRt,
  input  [4:0] IF_ID_RegisterRs,
  input  [4:0] IF_ID_RegisterRt,
  output PCWrite,
  output IF_IDWrite,
  output MUX
);

  wire comparator_1_eq, comparator_2_eq, or_1_out;

  Comparator #(.width(5), .mode("unsigned")) comparator_1 (
    .a(ID_EX_RegisterRt), .b(IF_ID_RegisterRs), .eq(comparator_1_eq));  // open: gt, lt
  Comparator #(.width(5), .mode("unsigned")) comparator_2 (
    .a(ID_EX_RegisterRt), .b(IF_ID_RegisterRt), .eq(comparator_2_eq));  // open: gt, lt
  or or_1 (or_1_out, comparator_1_eq, comparator_2_eq);
  not not_1 (PCWrite, IF_IDWrite);
  and and_1 (IF_IDWrite, ID_EX_MemRead, or_1_out);

  assign MUX = IF_IDWrite;
endmodule

module Forwarding_Unit__MEM (
  input  [4:0] WB_Address__in,
  input  WB_MemToReg__in,
  input  [4:0] MEM_Address__in,
  output MemDataSrc__out
);

  wire and_1_out, and_2_out, comparator_1_eq, comparator_2_eq, comparator_3_eq;

  Comparator #(.width(5), .mode("unsigned")) comparator_1 (
    .a(WB_Address__in), .b(MEM_Address__in), .eq(comparator_1_eq));  // open: gt, lt
  Comparator #(.width(5), .mode("unsigned")) comparator_2 (
    .a(WB_Address__in), .b({5{1'b0}}), .eq(comparator_2_eq));  // open: gt, lt
  Comparator #(.width(5), .mode("unsigned")) comparator_3 (
    .a(MEM_Address__in), .b({5{1'b0}}), .eq(comparator_3_eq));  // open: gt, lt
  and and_1 (and_1_out, ~comparator_2_eq, comparator_1_eq);  // AND_Gate
  and and_2 (and_2_out, comparator_1_eq, ~comparator_3_eq);  // AND_Gate
  and and_3 (MemDataSrc__out, WB_MemToReg__in, and_1_out, and_2_out);
endmodule

module Forwarding_Unit__ID (
  input  [4:0] ID_EX_RegDest__in,
  input  ID_EX_RegWrite__in,
  input  MEM_WB_RegWrite__in,
  input  [4:0] EX_MEM_RegDest__in,
  input  EX_MEM_RegWrite__in,
  input  [4:0] MEM_WB_RegDest__in,
  input  [4:0] rs__A__in,
  input  [4:0] rt__B__in,
  output [1:0] A__out,
  output [1:0] B__out
);

  wire and_1_out, and_2_out, and_3_out, and_4_out, and_5_out, and_6_out, comparator_1_eq, comparator_2_eq,
       comparator_3_eq, comparator_4_eq, comparator_5_eq, comparator_6_eq, comparator_7_eq, comparator_8_eq,
       comparator_9_eq, comparator_10_eq, comparator_11_eq, comparator_12_eq, not_1_out, not_2_out,
       not_3_out, not_4_out, not_5_out, not_6_out;
  wire [2:0] and_7_out, and_10_out;

  Comparator #(.width(5)) comparator_1 (.a(ID_EX_RegDest__in), .b(rs__A__in), .eq(comparator_1_eq));  // open: gt, lt
  not not_1 (not_1_out, comparator_2_eq);
  Comparator #(.width(5), .mode("unsigned")) comparator_2 (
    .a(ID_EX_RegDest__in), .b({5{1'b0}}), .eq(comparator_2_eq));  // open: gt, lt
  Comparator #(.width(5)) comparator_3 (.a(EX_MEM_RegDest__in), .b(rs__A__in), .eq(comparator_3_eq));  // open: gt, lt
  Comparator #(.width(5), .mode("unsigned")) comparator_4 (
    .a(EX_MEM_RegDest__in), .b({5{1'b0}}), .eq(comparator_4_eq));  // open: gt, lt
  not not_2 (not_2_out, comparator_4_eq);
  Comparator #(.width(5)) comparator_5 (.a(MEM_WB_RegDest__in), .b(rs__A__in), .eq(comparator_5_eq));  // open: gt, lt
  not not_3 (not_3_out, comparator_6_eq);
  Comparator #(.width(5), .mode("unsigned")) comparator_6 (
    .a(MEM_WB_RegDest__in), .b({5{1'b0}}), .eq(comparator_6_eq));  // open: gt, lt
  Comparator #(.width(5)) comparator_7 (.a(ID_EX_RegDest__in), .b(rt__B__in), .eq(comparator_7_eq));  // open: gt, lt
  not not_4 (not_4_out, comparator_8_eq);
  Comparator #(.width(5), .mode("unsigned")) comparator_8 (
    .a(ID_EX_RegDest__in), .b({5{1'b0}}), .eq(comparator_8_eq));  // open: gt, lt
  Comparator #(.width(5)) comparator_9 (.a(EX_MEM_RegDest__in), .b(rt__B__in), .eq(comparator_9_eq));  // open: gt, lt
  Comparator #(.width(5), .mode("unsigned")) comparator_10 (
    .a(EX_MEM_RegDest__in), .b({5{1'b0}}), .eq(comparator_10_eq));  // open: gt, lt
  not not_5 (not_5_out, comparator_10_eq);
  Comparator #(.width(5)) comparator_11 (.a(MEM_WB_RegDest__in), .b(rt__B__in), .eq(comparator_11_eq));  // open: gt, lt
  Comparator #(.width(5), .mode("unsigned")) comparator_12 (
    .a(MEM_WB_RegDest__in), .b({5{1'b0}}), .eq(comparator_12_eq));  // open: gt, lt
  not not_6 (not_6_out, comparator_12_eq);
  and and_1 (and_1_out, ID_EX_RegWrite__in, not_1_out);
  and and_2 (and_2_out, EX_MEM_RegWrite__in, not_2_out);
  and and_3 (and_3_out, MEM_WB_RegWrite__in, not_3_out);
  and and_4 (and_4_out, ID_EX_RegWrite__in, not_4_out);
  and and_5 (and_5_out, EX_MEM_RegWrite__in, not_5_out);
  and and_6 (and_6_out, MEM_WB_RegWrite__in, not_6_out);
  and and_7 (and_7_out[0], comparator_1_eq, and_1_out);
  and and_8 (and_7_out[1], comparator_3_eq, and_2_out);
  and and_9 (and_7_out[2], comparator_5_eq, and_3_out);
  and and_10 (and_10_out[0], comparator_7_eq, and_4_out);
  and and_11 (and_10_out[1], comparator_9_eq, and_5_out);
  and and_12 (and_10_out[2], comparator_11_eq, and_6_out);
  BranchForwardPLA branchforwardpla_1 (.in_1(and_7_out), .out_2(A__out));
  BranchForwardPLA branchforwardpla_2 (.in_1(and_10_out), .out_2(B__out));

  // Other names for the same wires on the sheet: A[4:0] = rs__A__in; B[4:0] = rt__B__in;
  //   EX_MEM_RegDest[4:0] = EX_MEM_RegDest__in; EX_MEM_RegWrite = EX_MEM_RegWrite__in;
  //   ID_EX_RegDest[4:0] = ID_EX_RegDest__in; ID_EX_RegWrite = ID_EX_RegWrite__in;
  //   MEM_WB_RegDest[4:0] = MEM_WB_RegDest__in; MEM_WB_RegWrite = MEM_WB_RegWrite__in
endmodule

module Hazard_detection_unit__branch (
  input  in_1,
  output PCWrite
);

  not not_1 (PCWrite, in_1);
endmodule

module Branch (
  input  [31:0] A__in,
  input  Branch,
  input  [31:0] B__in,
  input  [31:0] PC__in,
  input  [31:0] immediate__in,
  output BranchTaken,
  output [31:0] Out
);

  wire comparator_1_eq;
  wire [31:0] adder_1_p3, shifter_1_out;

  Comparator #(.width(32), .mode("unsigned")) comparator_1 (
    .a(A__in), .b(B__in), .eq(comparator_1_eq));  // open: gt, lt
  Shifter #(.width(32)) shifter_1 (.in(immediate__in), .\dist (5'b00010), .out(shifter_1_out));
  // Adder adder_1: pin names not known; wires that end beside it: PC__in, shifter_1_out, adder_1_p3
  and and_1 (BranchTaken, Branch, comparator_1_eq);
  Multiplexer #(.width(32), .enable("false")) multiplexer_1 (
    .in0(PC__in), .in1(adder_1_p3), .out(Out), .sel(BranchTaken));
endmodule

module BranchForwardPLA (
  input  [2:0] in_1,
  output [1:0] out_2
);

  // PLA pla_1: pin names not known; wires that end beside it: in_1, out_2
endmodule
