// Logisim project sandbox.circ as structural Verilog: 7 circuits, main circuit main
module main (
  output [31:0] Jump_Address,
  output [31:0] Fetched_Instruction,
  output Zero,
  output [31:0] A,
  output [31:0] A_2,
  output [31:0] B,
  output [31:0] B_2,
  output [31:0] Result,
  output [31:0] Next_Instruction,
  output [31:0] Data,
  output [5:0] Operation_Code,
  output [31:0] B_3,
  output [31:0] Result_2,
  output [31:0] _0_15,
  output [31:0] _0_15_2,
  output [3:0] out_16,
  output [31:0] Write_Back,
  output [1:0] out_18,
  output [2:0] out_19
);

  wire ALUSrc, and_1_out, Branch, id_ex_1_p2, Jump, JumpReg, MemRead, MemToReg, MemWrite, nor_1_out,
       not_1_out, not_2_out, not_3_out, RegDst, RegWrite, Tick;
  wire [3:0] alu_control_1_out_2, mips_alu_1_p3;
  wire [4:0] multiplexer_3_out, multiplexer_4_out;
  wire [23:0] bit_extender_3_out;
  wire [27:0] bit_extender_1_out, Control_p1;
  wire [31:0] adder_1_p3, adder_2_p4, adder_3_p2, adder_3_p3, id_ex_1_p5, multiplexer_1_out,
       multiplexer_2_out, multiplexer_5_out, multiplexer_7_out, multiplexer_8_out, multiplexer_9_out, PC_q;

  Multiplexer #(.width(32), .enable("false")) multiplexer_1 (
    .in0(multiplexer_9_out), .in1(adder_1_p3), .out(multiplexer_1_out), .sel(nor_1_out));
  nor nor_1 (nor_1_out, Jump, JumpReg);
  Register #(.width(32)) PC (.D(multiplexer_1_out), .Q(PC_q), .clk(Tick));  // open: en, clr
  // Adder adder_1: pin names not known; wires that end beside it: PC_q, 32'h4, adder_1_p3, adder_1_p3
  // Adder adder_2: pin names not known; wires that end beside it: PC_q, 32'h8, PC_q, adder_2_p4
  Clock clock_1 (.out(Tick));
  // MIPSProgramROM mipsprogramrom_1: pin names not known; wires that end beside it: Fetched_Instruction
  IF_ID if_id_1 (.Clock(Tick));  // open: PC__in, Inst___in, PC__out, Inst___out
  // PLA Control: pin names not known; wires that end beside it: {Jump_Address[31:28], Control_p1}, Fetched_Instruction[31:26]
  assign bit_extender_1_out = {{2{1'b0}}, Fetched_Instruction[25:0]};  // Bit_Extender bit_extender_1
  Multiplexer #(.width(32), .enable("false")) multiplexer_2 (
    .in0(adder_2_p4), .in1(Write_Back), .out(multiplexer_2_out), .sel(not_1_out));
  not not_1 (not_1_out, Jump);
  Shifter #(.width(28)) shifter_1 (.in(bit_extender_1_out), .\dist (5'b00010), .out(Jump_Address[27:0]));
  Multiplexer #(.width(5), .enable("false")) multiplexer_3 (
    .in0(multiplexer_4_out), .in1({5{1'b1}}), .out(multiplexer_3_out), .sel(Jump));
  Multiplexer #(.width(5), .enable("false")) multiplexer_4 (
    .in0(Fetched_Instruction[20:16]), .in1(Fetched_Instruction[15:11]), .out(multiplexer_4_out), .sel(RegDst));
  // RegisterFile registerfile_1: pin names not known; wires that end beside it: multiplexer_2_out, Tick, RegWrite, multiplexer_3_out, Fetched_Instruction[25:21], Fetched_Instruction[20:16], A, B
  assign _0_15 = {{16{Fetched_Instruction[15]}}, Fetched_Instruction[15:0]};  // Bit_Extender bit_extender_2
  // ID_EX id_ex_1: pin names not known; wires that end beside it: Jump_Address, id_ex_1_p2, Tick, id_ex_1_p2, id_ex_1_p5
  Multiplexer #(.width(32), .enable("false")) multiplexer_5 (
    .in0(B), .in1(_0_15), .out(multiplexer_5_out), .sel(ALUSrc));
  ALU_control alu_control_1 (.in_1({out_18, Fetched_Instruction[5:0]}), .out_2(alu_control_1_out_2));
  // Adder adder_3: pin names not known; wires that end beside it: {Jump_Address[31:28], Control_p1}, adder_3_p2, adder_3_p3
  Shifter #(.width(32)) shifter_2 (.in(_0_15), .\dist (5'b00010), .out(adder_3_p2));
  // MIPS_ALU mips_alu_1: pin names not known; wires that end beside it: A, multiplexer_5_out, mips_alu_1_p3, Zero, Result
  Multiplexer #(.width(4), .enable("false")) multiplexer_6 (
    .in0(alu_control_1_out_2), .in1(out_16), .out(mips_alu_1_p3), .sel(alu_control_1_out_2[3]));
  Imm__Ctrl imm_ctrl_1 (.in_1(Fetched_Instruction[28:26]), .out_2(out_16));
  Multiplexer #(.width(32), .enable("false")) multiplexer_7 (
    .in0({Jump_Address[31:28], Control_p1}), .in1(adder_3_p3), .out(multiplexer_7_out), .sel(and_1_out));
  and and_1 (and_1_out, Branch, Zero);
  Multiplexer #(.width(32), .enable("false")) multiplexer_8 (
    .in0(id_ex_1_p5), .in1(multiplexer_7_out), .out(multiplexer_8_out), .sel(not_2_out));
  not not_2 (not_2_out, Jump);
  Multiplexer #(.width(32), .enable("false")) multiplexer_9 (
    .in0(multiplexer_8_out), .in1(Result), .out(multiplexer_9_out), .sel(JumpReg));
  Comparator #(.width(6)) comparator_1 (.a(6'b001000), .b(Fetched_Instruction[5:0]), .eq(JumpReg));  // open: gt, lt
  EX_MEM ex_mem_1 (.Clock(Tick));  // open: PC__in, Zero__in, Result__in, Inst___in, PC__out, Zero__out, Result__out, inst___out
  Bit_Extender #(.in_width(32), .out_width(24)) bit_extender_3 (.in(Result), .out(bit_extender_3_out));
  // MIPS_RAM mips_ram_1: pin names not known; wires that end beside it: bit_extender_3_out, B, MemWrite, MemRead, Tick, Data
  MEM_WB mem_wb_1 (.Clock(Tick));  // open: Read_Data__in, Address__in, Read_Data__out, Address__out
  Multiplexer #(.width(32), .enable("false")) multiplexer_10 (
    .in0(Data), .in1(Result), .out(Write_Back), .sel(not_3_out));
  not not_3 (not_3_out, MemToReg);

  assign _0_15_2 = _0_15;
  assign A_2 = A;
  assign B_2 = B;
  assign B_3 = B;
  assign Next_Instruction = Fetched_Instruction;
  assign Operation_Code = Fetched_Instruction[31:26];
  assign out_19 = Fetched_Instruction[28:26];
  assign Result_2 = Result;

  // Other names for the same wires on the sheet: ALUOp[1:0] = out_18
endmodule

module ALU_control (
  input  [7:0] in_1,
  output [3:0] out_2
);

  // PLA pla_1: pin names not known; wires that end beside it: in_1, out_2
endmodule

module Imm__Ctrl (
  input  [2:0] in_1,
  output [3:0] out_2
);

  // PLA Imm__Ctrl: pin names not known; wires that end beside it: in_1, out_2
endmodule

module IF_ID (
  input  Clock,
  input  [31:0] PC__in,
  input  [31:0] Inst___in,
  output [31:0] PC__out,
  output [31:0] Inst___out
);

  Register #(.width(32)) register_1 (.D(PC__in), .Q(PC__out), .clk(Clock));  // open: en, clr
  Register #(.width(32)) register_2 (.D(Inst___in), .Q(Inst___out), .clk(Clock));  // open: en, clr

  // Other names for the same wires on the sheet: Tick = Clock
endmodule

module ID_EX (
  input  Clock,
  input  [31:0] PC__in,
  input  [31:0] A__in,
  input  [31:0] B__in,
  input  [31:0] Inst___in,
  input  MemToReg__in,
  input  RegDst__in,
  input  MemRead__in,
  input  MemWrite__in,
  input  ALUSrc__in,
  input  Branch__in,
  input  [1:0] ALUOp__in,
  input  Jump__in,
  input  JumpReg__in,
  output [31:0] PC__out,
  output [31:0] A__out,
  output [31:0] B__out,
  output [31:0] inst___out,
  output MemToReg__out,
  output RegDst__out,
  output MemRead__out,
  output MemWrite__out,
  output ALUSrc__out,
  output Branch__out,
  output [1:0] ALUOp__out,
  output Jump__out,
  output JumpReg__out
);

  Register #(.width(32)) register_1 (.D(PC__in), .Q(PC__out), .clk(Clock));  // open: en, clr
  Register #(.width(32)) register_2 (.D(A__in), .Q(A__out), .clk(Clock));  // open: en, clr
  Register #(.width(32)) register_3 (.D(B__in), .Q(B__out), .clk(Clock));  // open: en, clr
  Register #(.width(32)) register_4 (.D(Inst___in), .Q(inst___out), .clk(Clock));  // open: en, clr
  Register #(.width(1)) register_5 (.D(MemToReg__in), .Q(MemToReg__out), .clk(Clock));  // open: en, clr
  Register #(.width(1)) register_6 (.D(RegDst__in), .Q(RegDst__out), .clk(Clock));  // open: en, clr
  Register #(.width(1)) register_7 (.D(MemRead__in), .Q(MemRead__out), .clk(Clock));  // open: en, clr
  Register #(.width(1)) register_8 (.D(MemWrite__in), .Q(MemWrite__out), .clk(Clock));  // open: en, clr
  Register #(.width(1)) register_9 (.D(ALUSrc__in), .Q(ALUSrc__out), .clk(Clock));  // open: en, clr
  Register #(.width(1)) register_10 (.D(Branch__in), .Q(Branch__out), .clk(Clock));  // open: en, clr
  Register #(.width(2)) register_11 (.D(ALUOp__in), .Q(ALUOp__out), .clk(Clock));  // open: en, clr
  Register #(.width(1)) register_12 (.D(Jump__in), .Q(Jump__out), .clk(Clock));  // open: en, clr
  Register #(.width(1)) register_13 (.D(JumpReg__in), .Q(JumpReg__out), .clk(Clock));  // open: en, clr

  // Other names for the same wires on the sheet: Tick = Clock

  // Notes on the sheet:
  //   WB
  //   M
  //   EX
endmodule

module EX_MEM (
  input  Clock,
  input  [31:0] PC__in,
  input  Zero__in,
  input  [31:0] Result__in,
  input  [31:0] Inst___in,
  output [31:0] PC__out,
  output Zero__out,
  output [31:0] Result__out,
  output [31:0] inst___out
);

  Register #(.width(32)) register_1 (.D(PC__in), .Q(PC__out), .clk(Clock));  // open: en, clr
  Register #(.width(1)) register_2 (.D(Zero__in), .Q(Zero__out), .clk(Clock));  // open: en, clr
  Register #(.width(32)) register_3 (.D(Result__in), .Q(Result__out), .clk(Clock));  // open: en, clr
  Register #(.width(32)) register_4 (.D(Inst___in), .Q(inst___out), .clk(Clock));  // open: en, clr

  // Other names for the same wires on the sheet: Tick = Clock
endmodule

module MEM_WB (
  input  Clock,
  input  [31:0] Read_Data__in,
  input  [31:0] Address__in,
  output [31:0] Read_Data__out,
  output [31:0] Address__out
);

  Register #(.width(32)) register_1 (.D(Read_Data__in), .Q(Read_Data__out), .clk(Clock));  // open: en, clr
  Register #(.width(32)) register_2 (.D(Address__in), .Q(Address__out), .clk(Clock));  // open: en, clr

  // Other names for the same wires on the sheet: Tick = Clock
endmodule
